# Fritzing sketch helmet_Sender_circuit_Diagram (saved by Fritzing 0.8.7b)

parts:
  U1 = ESP32-38PinWide [part_number=ESP32-38PinWide]
  J1 = Basic Force Sensing Resistor (FSR) [package=THT]
  J2 = Basic Force Sensing Resistor (FSR) [package=THT]
  R2 = Resistor [tolerance=±5% resistance=10k package=THT]
  R3 = Resistor [tolerance=±5% resistance=10k package=THT]
  Transceiver1 = nRF24L01 [package=module]
  Part1 = MQ-4
  C1 = Capacitor Polarized [package=panasonic_c]
  R4 = Resistor [tolerance=±5% resistance=220 package=THT]

nets:
  N1: U1.3.3, J1.pin_0
  N2: U1.GPIO35, Part1.AO, R4.Pin_1
  N3: U1.GPIO32, J2.pin_1, R3.Pin_1
  N4: U1.GPIO33, J1.pin_1, R2.Pin_1
  N5: U1.GPIO26, Transceiver1.CE
  N6: U1.GPIO27, Transceiver1.CSN
  N7: U1.GPIO14, Transceiver1.SCK
  N8: U1.GPIO12, Transceiver1.MOSI
  N9: U1.GPIO11, Transceiver1.GND, C1.-

custom parts:
  ESP32-38PinWide: Generic 38-Pin ESP32 with wide format (only access to one side of pins on a breadboard) based on Stephen Lilley's HiLetgo ESP-WROOM-32 ESP32 ESP-32S Development Board.
  nRF24L01: nRF24L01 module
